# Fritzing sketch Controller (saved by Fritzing 0.7.5b)
breadboards: 1

parts:
  LCD1 = LCD screen
  U1 = atmega328 [package=dip]
  XTAL1 = Crystal [frequency="16 Mhz" package=THT]
  C1 = Ceramic Capacitor [capacitance=22pF package="100 mil [THT, multilayer]"]
  C2 = Ceramic Capacitor [capacitance=22pF package="100 mil [THT, multilayer]"]
  R1 = Rotary Potentiometer (Small) [maximum_resistance=100kΩ]
  R2 = Resistor [tolerance=±5% resistance=220 package=THT]
  S2 = Pushbutton [package="[THT]"]
  R5 = Resistor [tolerance=±5% resistance=10k package=THT]
  R6 = Resistor [tolerance=±5% resistance=100 package=THT]
  S3 = Pushbutton [package="[THT]"]
  R7 = Resistor [tolerance=±5% resistance=10k package=THT]
  R8 = Resistor [tolerance=±5% resistance=100 package=THT]
  S4 = Pushbutton [package="[THT]"]
  R9 = Resistor [tolerance=±5% resistance=10k package=THT]
  R10 = Resistor [tolerance=±5% resistance=100 package=THT]
  S5 = Pushbutton [package="[THT]"]
  R11 = Resistor [tolerance=±5% resistance=10k package=THT]
  R12 = Resistor [tolerance=±5% resistance=100 package=THT]
  LED1 = LED - 5mm [color="Red (633nm)" package="5 mm [THT]"]

nets:
  GND: LCD1.VSS, LCD1.RS, LCD1.LED-, U1.GND, U1.D12, C1.1, C2.1, R1.leg1, S2.Pin_3, S2.Pin_4, S3.Pin_4, S4.Pin_3, S4.Pin_4, S5.Pin_4, LED1.cathode
  5V: LCD1.VDD, U1.VCC, U1.AVCC, U1.AREF, R1.leg2, R2.Pin_1, R5.Pin_0, R7.Pin_0, R9.Pin_0, R11.Pin_0
  N1: LCD1.V0, R1.wiper
  N2: LCD1.E, U1.D11_(PWM)
  N3: LCD1.DB4, U1.A5
  N4: LCD1.DB5, U1.A4
  N5: LCD1.DB6, U1.A3
  N6: LCD1.DB7, U1.A2
  N7: LCD1.LED+, R2.Pin_0
  N8: U1.XLAT1, XTAL1.pin_0, C1.0
  N9: U1.XLAT2, XTAL1.pin_1, C2.0
  N10: U1.D6_(PWM), LED1.anode
  N11: U1.D7, R10.Pin_1
  N12: U1.D8, R12.Pin_0
  N13: U1.D9_(PWM), R8.Pin_0
  N14: U1.D10_(PWM), R6.Pin_0
  N15: S2.Pin_1, S2.Pin_2, R5.Pin_1, R6.Pin_1
  N16: S3.Pin_1, S3.Pin_2, R7.Pin_1, R8.Pin_1
  N17: S4.Pin_1, S4.Pin_2, R9.Pin_1, R10.Pin_0
  N18: S5.Pin_1, S5.Pin_2, R11.Pin_1, R12.Pin_1
